# Fritzing sketch sensor-node (saved by Fritzing 0.8.3b)

parts:
  Bauteil1 = Arduino Pro Mini v13
  RHT1 = Humidity and Temperature Sensor RHT03
  Bauteil2 = Barometric Pressure Sensor - BMP180 Breakout (GY-68)
  U1 = CHJ-FST1000M [package=CHJ-FST1000M]
  R1 = Resistor [tolerance=±5% resistance=4.7k package="0603 [SMD]"]

nets:
  N1: Bauteil1.DTR, RHT1.GND_2, Bauteil2.GND
  N2: Bauteil1.A4, Bauteil2.SDA
  N3: Bauteil1.A5, Bauteil2.SCL
  GND: Bauteil1.GND, U1.GND
  VCC: Bauteil1.VCC, U1.+5V
  N4: Bauteil1.A3, U1.DATA
  N5: Bauteil1.A0, RHT1.Data-signal
  N6: Bauteil1.D13/SCK, RHT1.Vcc
  N7: Bauteil1.D7, Bauteil1.D6_PWM, R1.Pin_0
  N8: Bauteil1.D5_PWM, Bauteil2.VCC
  N9: Bauteil1.D4, R1.Pin_1

custom parts:
  CHJ-FST1000M: RF LINK
